// Digital circuit 10x16 Ram.dig as structural Verilog
module _10x16_Ram (
  input  CLK,
  input  [15:0] WRD_15_0,
  input  [3:0] WR_3_0,
  input  [3:0] RA2_3_0,
  input  [3:0] RA1_3_0,
  input  WE,
  output [15:0] RD1_15_0,
  output [15:0] RD2_15_0
);

  wire and_1_out, and_2_out, and_3_out, and_4_out, and_5_out, and_6_out, and_7_out, and_8_out, and_9_out,
       and_10_out, decoder_1_out_0, decoder_1_out_1, decoder_1_out_2, decoder_1_out_3, decoder_1_out_4,
       decoder_1_out_5, decoder_1_out_6, decoder_1_out_7, decoder_1_out_8, decoder_1_out_9, decoder_2_out_0,
       decoder_2_out_1, decoder_2_out_2, decoder_2_out_3, decoder_2_out_4, decoder_2_out_5, decoder_2_out_6,
       decoder_2_out_7, decoder_2_out_8, decoder_2_out_9, decoder_3_out_0, decoder_3_out_1, decoder_3_out_2,
       decoder_3_out_3, decoder_3_out_4, decoder_3_out_5, decoder_3_out_6, decoder_3_out_7, decoder_3_out_8,
       decoder_3_out_9;
  wire [15:0] _1x16_ram_1_rd1_15_0, _1x16_ram_1_rd2_15_0, _1x16_ram_2_rd1_15_0, _1x16_ram_2_rd2_15_0,
       _1x16_ram_3_rd1_15_0, _1x16_ram_3_rd2_15_0, _1x16_ram_4_rd1_15_0, _1x16_ram_4_rd2_15_0,
       _1x16_ram_5_rd1_15_0, _1x16_ram_5_rd2_15_0, _1x16_ram_6_rd1_15_0, _1x16_ram_6_rd2_15_0,
       _1x16_ram_7_rd1_15_0, _1x16_ram_7_rd2_15_0, _1x16_ram_8_rd1_15_0, _1x16_ram_8_rd2_15_0,
       _1x16_ram_9_rd1_15_0, _1x16_ram_9_rd2_15_0, _1x16_ram_10_rd1_15_0, _1x16_ram_10_rd2_15_0, or_1_out,
       or_2_out, or_3_out, or_4_out;

  Decoder #(.Selector_Bits(4)) decoder_1 (
    .sel(WR_3_0), .out_0(decoder_1_out_0), .out_1(decoder_1_out_1), .out_2(decoder_1_out_2),
    .out_3(decoder_1_out_3), .out_4(decoder_1_out_4), .out_5(decoder_1_out_5), .out_6(decoder_1_out_6),
    .out_7(decoder_1_out_7), .out_8(decoder_1_out_8), .out_9(decoder_1_out_9));  // open: out_10, out_11, out_12, out_13, out_14, out_15
  Decoder #(.Selector_Bits(4)) decoder_2 (
    .sel(RA1_3_0), .out_0(decoder_2_out_0), .out_1(decoder_2_out_1), .out_2(decoder_2_out_2),
    .out_3(decoder_2_out_3), .out_4(decoder_2_out_4), .out_5(decoder_2_out_5), .out_6(decoder_2_out_6),
    .out_7(decoder_2_out_7), .out_8(decoder_2_out_8), .out_9(decoder_2_out_9));  // open: out_10, out_11, out_12, out_13, out_14, out_15
  Decoder #(.Selector_Bits(4)) decoder_3 (
    .sel(RA2_3_0), .out_0(decoder_3_out_0), .out_1(decoder_3_out_1), .out_2(decoder_3_out_2),
    .out_3(decoder_3_out_3), .out_4(decoder_3_out_4), .out_5(decoder_3_out_5), .out_6(decoder_3_out_6),
    .out_7(decoder_3_out_7), .out_8(decoder_3_out_8), .out_9(decoder_3_out_9));  // open: out_10, out_11, out_12, out_13, out_14, out_15
  and and_1 (and_1_out, decoder_1_out_0, WE);
  and and_2 (and_2_out, decoder_1_out_1, WE);
  and and_3 (and_3_out, decoder_1_out_2, WE);
  and and_4 (and_4_out, decoder_1_out_3, WE);
  and and_5 (and_5_out, decoder_1_out_4, WE);
  and and_6 (and_6_out, decoder_1_out_5, WE);
  and and_7 (and_7_out, decoder_1_out_6, WE);
  and and_8 (and_8_out, decoder_1_out_7, WE);
  and and_9 (and_9_out, decoder_1_out_8, WE);
  and and_10 (and_10_out, decoder_1_out_9, WE);
  _1x16_Ram _1x16_ram_1 (
    .WD_15_0(WRD_15_0), .WS(and_1_out), .RS1(decoder_2_out_0), .RS2(decoder_3_out_0), .CLK(CLK),
    .RD1_15_0(_1x16_ram_1_rd1_15_0), .RD2_15_0(_1x16_ram_1_rd2_15_0));
  _1x16_Ram _1x16_ram_2 (
    .WD_15_0(WRD_15_0), .WS(and_2_out), .RS1(decoder_2_out_1), .RS2(decoder_3_out_1), .CLK(CLK),
    .RD1_15_0(_1x16_ram_2_rd1_15_0), .RD2_15_0(_1x16_ram_2_rd2_15_0));
  _1x16_Ram _1x16_ram_3 (
    .WD_15_0(WRD_15_0), .WS(and_3_out), .RS1(decoder_2_out_2), .RS2(decoder_3_out_2), .CLK(CLK),
    .RD1_15_0(_1x16_ram_3_rd1_15_0), .RD2_15_0(_1x16_ram_3_rd2_15_0));
  _1x16_Ram _1x16_ram_4 (
    .WD_15_0(WRD_15_0), .WS(and_4_out), .RS1(decoder_2_out_3), .RS2(decoder_3_out_3), .CLK(CLK),
    .RD1_15_0(_1x16_ram_4_rd1_15_0), .RD2_15_0(_1x16_ram_4_rd2_15_0));
  _1x16_Ram _1x16_ram_5 (
    .WD_15_0(WRD_15_0), .WS(and_5_out), .RS1(decoder_2_out_4), .RS2(decoder_3_out_4), .CLK(CLK),
    .RD1_15_0(_1x16_ram_5_rd1_15_0), .RD2_15_0(_1x16_ram_5_rd2_15_0));
  _1x16_Ram _1x16_ram_6 (
    .WD_15_0(WRD_15_0), .WS(and_6_out), .RS1(decoder_2_out_5), .RS2(decoder_3_out_5), .CLK(CLK),
    .RD1_15_0(_1x16_ram_6_rd1_15_0), .RD2_15_0(_1x16_ram_6_rd2_15_0));
  _1x16_Ram _1x16_ram_7 (
    .WD_15_0(WRD_15_0), .WS(and_7_out), .RS1(decoder_2_out_6), .RS2(decoder_3_out_6), .CLK(CLK),
    .RD1_15_0(_1x16_ram_7_rd1_15_0), .RD2_15_0(_1x16_ram_7_rd2_15_0));
  _1x16_Ram _1x16_ram_8 (
    .WD_15_0(WRD_15_0), .WS(and_8_out), .RS1(decoder_2_out_7), .RS2(decoder_3_out_7), .CLK(CLK),
    .RD1_15_0(_1x16_ram_8_rd1_15_0), .RD2_15_0(_1x16_ram_8_rd2_15_0));
  _1x16_Ram _1x16_ram_9 (
    .WD_15_0(WRD_15_0), .WS(and_9_out), .RS1(decoder_2_out_8), .RS2(decoder_3_out_8), .CLK(CLK),
    .RD1_15_0(_1x16_ram_9_rd1_15_0), .RD2_15_0(_1x16_ram_9_rd2_15_0));
  _1x16_Ram _1x16_ram_10 (
    .WD_15_0(WRD_15_0), .WS(and_10_out), .RS1(decoder_2_out_9), .RS2(decoder_3_out_9), .CLK(CLK),
    .RD1_15_0(_1x16_ram_10_rd1_15_0), .RD2_15_0(_1x16_ram_10_rd2_15_0));
  assign or_1_out = _1x16_ram_1_rd1_15_0 | _1x16_ram_2_rd1_15_0 | _1x16_ram_3_rd1_15_0 | _1x16_ram_4_rd1_15_0 | _1x16_ram_5_rd1_15_0;  // Or or_1, 16 bits wide
  assign or_2_out = _1x16_ram_6_rd1_15_0 | _1x16_ram_7_rd1_15_0 | _1x16_ram_8_rd1_15_0 | _1x16_ram_9_rd1_15_0 | _1x16_ram_10_rd1_15_0;  // Or or_2, 16 bits wide
  assign or_3_out = _1x16_ram_1_rd2_15_0 | _1x16_ram_2_rd2_15_0 | _1x16_ram_3_rd2_15_0 | _1x16_ram_4_rd2_15_0 | _1x16_ram_5_rd2_15_0;  // Or or_3, 16 bits wide
  assign or_4_out = _1x16_ram_6_rd2_15_0 | _1x16_ram_7_rd2_15_0 | _1x16_ram_8_rd2_15_0 | _1x16_ram_9_rd2_15_0 | _1x16_ram_10_rd2_15_0;  // Or or_4, 16 bits wide
  assign RD1_15_0 = or_1_out | or_2_out;  // Or or_5, 16 bits wide
  assign RD2_15_0 = or_3_out | or_4_out;  // Or or_6, 16 bits wide
endmodule
