// Digital circuit 1x16 Ram.dig as structural Verilog
module _1x16_Ram (
  input  WS,
  input  RS1,
  input  RS2,
  input  CLK,
  input  [15:0] WD_15_0,
  output [15:0] RD1_15_0,
  output [15:0] RD2_15_0
);

  _1_Bit_Ram _1_bit_ram_1 (
    .WD(WD_15_0[0]), .WS(WS), .RS1(RS1), .RS2(RS2), .CLK(CLK), .RD1(RD1_15_0[0]), .RD2(RD2_15_0[0]));
  _1_Bit_Ram _1_bit_ram_2 (
    .WD(WD_15_0[1]), .WS(WS), .RS1(RS1), .RS2(RS2), .CLK(CLK), .RD1(RD1_15_0[1]), .RD2(RD2_15_0[1]));
  _1_Bit_Ram _1_bit_ram_3 (
    .WD(WD_15_0[2]), .WS(WS), .RS1(RS1), .RS2(RS2), .CLK(CLK), .RD1(RD1_15_0[2]), .RD2(RD2_15_0[2]));
  _1_Bit_Ram _1_bit_ram_4 (
    .WD(WD_15_0[3]), .WS(WS), .RS1(RS1), .RS2(RS2), .CLK(CLK), .RD1(RD1_15_0[3]), .RD2(RD2_15_0[3]));
  _1_Bit_Ram _1_bit_ram_5 (
    .WD(WD_15_0[4]), .WS(WS), .RS1(RS1), .RS2(RS2), .CLK(CLK), .RD1(RD1_15_0[4]), .RD2(RD2_15_0[4]));
  _1_Bit_Ram _1_bit_ram_6 (
    .WD(WD_15_0[5]), .WS(WS), .RS1(RS1), .RS2(RS2), .CLK(CLK), .RD1(RD1_15_0[5]), .RD2(RD2_15_0[5]));
  _1_Bit_Ram _1_bit_ram_7 (
    .WD(WD_15_0[6]), .WS(WS), .RS1(RS1), .RS2(RS2), .CLK(CLK), .RD1(RD1_15_0[6]), .RD2(RD2_15_0[6]));
  _1_Bit_Ram _1_bit_ram_8 (
    .WD(WD_15_0[7]), .WS(WS), .RS1(RS1), .RS2(RS2), .CLK(CLK), .RD1(RD1_15_0[7]), .RD2(RD2_15_0[7]));
  _1_Bit_Ram _1_bit_ram_9 (
    .WD(WD_15_0[8]), .WS(WS), .RS1(RS1), .RS2(RS2), .CLK(CLK), .RD1(RD1_15_0[8]), .RD2(RD2_15_0[8]));
  _1_Bit_Ram _1_bit_ram_10 (
    .WD(WD_15_0[9]), .WS(WS), .RS1(RS1), .RS2(RS2), .CLK(CLK), .RD1(RD1_15_0[9]), .RD2(RD2_15_0[9]));
  _1_Bit_Ram _1_bit_ram_11 (
    .WD(WD_15_0[10]), .WS(WS), .RS1(RS1), .RS2(RS2), .CLK(CLK), .RD1(RD1_15_0[10]), .RD2(RD2_15_0[10]));
  _1_Bit_Ram _1_bit_ram_12 (
    .WD(WD_15_0[11]), .WS(WS), .RS1(RS1), .RS2(RS2), .CLK(CLK), .RD1(RD1_15_0[11]), .RD2(RD2_15_0[11]));
  _1_Bit_Ram _1_bit_ram_13 (
    .WD(WD_15_0[12]), .WS(WS), .RS1(RS1), .RS2(RS2), .CLK(CLK), .RD1(RD1_15_0[12]), .RD2(RD2_15_0[12]));
  _1_Bit_Ram _1_bit_ram_14 (
    .WD(WD_15_0[13]), .WS(WS), .RS1(RS1), .RS2(RS2), .CLK(CLK), .RD1(RD1_15_0[13]), .RD2(RD2_15_0[13]));
  _1_Bit_Ram _1_bit_ram_15 (
    .WD(WD_15_0[14]), .WS(WS), .RS1(RS1), .RS2(RS2), .CLK(CLK), .RD1(RD1_15_0[14]), .RD2(RD2_15_0[14]));
  _1_Bit_Ram _1_bit_ram_16 (
    .WD(WD_15_0[15]), .WS(WS), .RS1(RS1), .RS2(RS2), .CLK(CLK), .RD1(RD1_15_0[15]), .RD2(RD2_15_0[15]));
endmodule
