// Digital circuit 4 Bit Reg.dig as structural Verilog
module _4_Bit_Reg (
  input  [3:0] In_3_0,
  input  CLK,
  output [3:0] Out_3_0
);

  _1_Bit_Reg _1_bit_reg_1 (.Din(In_3_0[3]), .Sel(1'b1), .CLK(CLK), .Dout(Out_3_0[3]));
  _1_Bit_Reg _1_bit_reg_2 (.Din(In_3_0[2]), .Sel(1'b1), .CLK(CLK), .Dout(Out_3_0[2]));
  _1_Bit_Reg _1_bit_reg_3 (.Din(In_3_0[1]), .Sel(1'b1), .CLK(CLK), .Dout(Out_3_0[1]));
  _1_Bit_Reg _1_bit_reg_4 (.Din(In_3_0[0]), .Sel(1'b1), .CLK(CLK), .Dout(Out_3_0[0]));
endmodule
