// Digital circuit 6 Bit ALU.dig as structural Verilog
module _6_Bit_ALU (
  input  [1:0] OP_1_0,
  input  [5:0] A_5_0,
  input  [5:0] B_5_0,
  output [5:0] O_5_0,
  output CF
);

  wire [5:0] _6_bit_adder_1_s_5_0, _6_bit_and_1_o_5_0, _6_bit_shr_1_o_5_0;

  _6_Bit_Adder _6_bit_adder_1 (.A_5_0(A_5_0), .B_5_0(B_5_0), .S_5_0(_6_bit_adder_1_s_5_0), .Cout(CF));
  _6_Bit_And _6_bit_and_1 (.A_5_0(A_5_0), .B_5_0(B_5_0), .O_5_0(_6_bit_and_1_o_5_0));
  _6_Bit_SHR _6_bit_shr_1 (.A_5_0(A_5_0), .B_5_0(B_5_0), .O_5_0(_6_bit_shr_1_o_5_0));
  Multiplexer #(.Selector_Bits(2), .Bits(6)) multiplexer_1 (
    .sel(OP_1_0), .in_0(_6_bit_adder_1_s_5_0), .in_1(_6_bit_and_1_o_5_0), .in_2(_6_bit_shr_1_o_5_0),
    .in_3({6{1'b0}}), .out(O_5_0));
endmodule
