// Digital circuit 6 Bit Adder.dig as structural Verilog
module _6_Bit_Adder (
  input  [5:0] A_5_0,
  input  [5:0] B_5_0,
  output [5:0] S_5_0,
  output Cout
);

  wire fa_2_cout, fa_3_cout, fa_4_cout, fa_5_cout, fa_6_cout;

  FA fa_1 (.Y(B_5_0[5]), .X(A_5_0[5]), .Cout(Cout), .S(S_5_0[5]), .Cin(fa_2_cout));
  FA fa_2 (.Y(B_5_0[4]), .X(A_5_0[4]), .Cout(fa_2_cout), .S(S_5_0[4]), .Cin(fa_3_cout));
  FA fa_3 (.Y(B_5_0[3]), .X(A_5_0[3]), .Cout(fa_3_cout), .S(S_5_0[3]), .Cin(fa_4_cout));
  FA fa_4 (.Y(B_5_0[2]), .X(A_5_0[2]), .Cout(fa_4_cout), .S(S_5_0[2]), .Cin(fa_5_cout));
  FA fa_5 (.Y(B_5_0[1]), .X(A_5_0[1]), .Cout(fa_5_cout), .S(S_5_0[1]), .Cin(fa_6_cout));
  FA fa_6 (.Y(B_5_0[0]), .X(A_5_0[0]), .Cout(fa_6_cout), .S(S_5_0[0]), .Cin(1'b0));
endmodule
