// Digital circuit 6 Bit And.dig as structural Verilog
module _6_Bit_And (
  input  [5:0] A_5_0,
  input  [5:0] B_5_0,
  output [5:0] O_5_0
);

  and and_1 (O_5_0[5], A_5_0[5], B_5_0[5]);
  and and_2 (O_5_0[4], A_5_0[4], B_5_0[4]);
  and and_3 (O_5_0[3], A_5_0[3], B_5_0[3]);
  and and_4 (O_5_0[2], A_5_0[2], B_5_0[2]);
  and and_5 (O_5_0[1], A_5_0[1], B_5_0[1]);
  and and_6 (O_5_0[0], A_5_0[0], B_5_0[0]);
endmodule
