// Digital circuit 6 Bit Reg Set.dig as structural Verilog
module _6_Bit_Reg_Set (
  input  [1:0] WR_1_0,
  input  [5:0] WRD_5_0,
  input  WE,
  input  CLK,
  input  [1:0] RA_1_0,
  input  [1:0] RB_1_0,
  output [5:0] A_5_0,
  output [5:0] B_5_0
);

  wire and_1_out, and_2_out, and_3_out, decoder_1_out_0, decoder_1_out_1, decoder_1_out_2;
  wire [5:0] _6_bit_reg_1_dout_5_0, _6_bit_reg_2_dout_5_0, _6_bit_reg_3_dout_5_0;

  Decoder #(.Selector_Bits(2)) decoder_1 (
    .sel(WR_1_0), .out_0(decoder_1_out_0), .out_1(decoder_1_out_1), .out_2(decoder_1_out_2));  // open: out_3
  and and_1 (and_1_out, WE, decoder_1_out_0);
  and and_2 (and_2_out, WE, decoder_1_out_1);
  and and_3 (and_3_out, WE, decoder_1_out_2);
  _6_Bit_Reg _6_bit_reg_1 (.Din_5_0(WRD_5_0), .Sel(and_1_out), .CLK(CLK), .Dout_5_0(_6_bit_reg_1_dout_5_0));
  _6_Bit_Reg _6_bit_reg_2 (.Din_5_0(WRD_5_0), .Sel(and_2_out), .CLK(CLK), .Dout_5_0(_6_bit_reg_2_dout_5_0));
  _6_Bit_Reg _6_bit_reg_3 (.Din_5_0(WRD_5_0), .Sel(and_3_out), .CLK(CLK), .Dout_5_0(_6_bit_reg_3_dout_5_0));
  Multiplexer #(.Selector_Bits(2), .Bits(6)) multiplexer_1 (
    .sel(RA_1_0), .in_0(_6_bit_reg_1_dout_5_0), .in_1(_6_bit_reg_2_dout_5_0), .in_2(_6_bit_reg_3_dout_5_0),
    .in_3({6{1'b0}}), .out(A_5_0));
  Multiplexer #(.Selector_Bits(2), .Bits(6)) multiplexer_2 (
    .sel(RB_1_0), .in_0(_6_bit_reg_1_dout_5_0), .in_1(_6_bit_reg_2_dout_5_0), .in_2(_6_bit_reg_3_dout_5_0),
    .in_3({6{1'b0}}), .out(B_5_0));
endmodule
