// Digital circuit 6 Bit Reg.dig as structural Verilog
module _6_Bit_Reg (
  input  [5:0] Din_5_0,
  input  Sel,
  input  CLK,
  output [5:0] Dout_5_0
);

  _1_Bit_Reg _1_bit_reg_1 (.Din(Din_5_0[0]), .Sel(Sel), .CLK(CLK), .Dout(Dout_5_0[0]));
  _1_Bit_Reg _1_bit_reg_2 (.Din(Din_5_0[1]), .Sel(Sel), .CLK(CLK), .Dout(Dout_5_0[1]));
  _1_Bit_Reg _1_bit_reg_3 (.Din(Din_5_0[2]), .Sel(Sel), .CLK(CLK), .Dout(Dout_5_0[2]));
  _1_Bit_Reg _1_bit_reg_4 (.Din(Din_5_0[3]), .Sel(Sel), .CLK(CLK), .Dout(Dout_5_0[3]));
  _1_Bit_Reg _1_bit_reg_5 (.Din(Din_5_0[4]), .Sel(Sel), .CLK(CLK), .Dout(Dout_5_0[4]));
  _1_Bit_Reg _1_bit_reg_6 (.Din(Din_5_0[5]), .Sel(Sel), .CLK(CLK), .Dout(Dout_5_0[5]));
endmodule
