// Digital circuit 6 Bit SHR.dig as structural Verilog
module _6_Bit_SHR (
  input  [5:0] A_5_0,
  input  [5:0] B_5_0,
  output [5:0] O_5_0
);

  wire Sel;
  wire [5:0] multiplexer_2_out;

  or or_1 (Sel, B_5_0[3], B_5_0[4], B_5_0[5]);
  Multiplexer #(.Selector_Bits(3)) multiplexer_1 (
    .sel(B_5_0[2:0]), .in_0(A_5_0[5]), .in_1(1'b0), .in_2(1'b0), .in_3(1'b0), .in_4(1'b0), .in_5(1'b0),
    .in_6(1'b0), .in_7(1'b0), .out(multiplexer_2_out[5]));
  Multiplexer #(.Selector_Bits(3)) multiplexer_2 (
    .sel(B_5_0[2:0]), .in_0(A_5_0[4]), .in_1(A_5_0[5]), .in_2(1'b0), .in_3(1'b0), .in_4(1'b0), .in_5(1'b0),
    .in_6(1'b0), .in_7(1'b0), .out(multiplexer_2_out[4]));
  Multiplexer #(.Selector_Bits(3)) multiplexer_3 (
    .sel(B_5_0[2:0]), .in_0(A_5_0[3]), .in_1(A_5_0[4]), .in_2(A_5_0[5]), .in_3(1'b0), .in_4(1'b0),
    .in_5(1'b0), .in_6(1'b0), .in_7(1'b0), .out(multiplexer_2_out[3]));
  Multiplexer #(.Selector_Bits(3)) multiplexer_4 (
    .sel(B_5_0[2:0]), .in_0(A_5_0[2]), .in_1(A_5_0[3]), .in_2(A_5_0[4]), .in_3(A_5_0[5]), .in_4(1'b0),
    .in_5(1'b0), .in_6(1'b0), .in_7(1'b0), .out(multiplexer_2_out[2]));
  Multiplexer #(.Selector_Bits(3)) multiplexer_5 (
    .sel(B_5_0[2:0]), .in_0(A_5_0[1]), .in_1(A_5_0[2]), .in_2(A_5_0[3]), .in_3(A_5_0[4]), .in_4(A_5_0[5]),
    .in_5(1'b0), .in_6(1'b0), .in_7(1'b0), .out(multiplexer_2_out[1]));
  Multiplexer #(.Selector_Bits(3)) multiplexer_6 (
    .sel(B_5_0[2:0]), .in_0(A_5_0[0]), .in_1(A_5_0[1]), .in_2(A_5_0[2]), .in_3(A_5_0[3]), .in_4(A_5_0[4]),
    .in_5(A_5_0[5]), .in_6(1'b0), .in_7(1'b0), .out(multiplexer_2_out[0]));
  Multiplexer #(.Bits(6)) multiplexer_7 (.sel(Sel), .in_0(multiplexer_2_out), .in_1({6{1'b0}}), .out(O_5_0));

  // Other names for the same wires on the sheet: A0 = A_5_0[0]; A1 = A_5_0[1]; A2 = A_5_0[2]; A3 = A_5_0[3];
  //   A4 = A_5_0[4]; A5 = A_5_0[5]
endmodule
