// Digital circuit CPU.dig as structural Verilog
module CPU (
  input  CLK,
  input  [15:0] WRD_15_0,
  input  [3:0] WR_3_0,
  input  WE,
  input  EN,
  input  [3:0] RA2_3_0,
  input  ZF,
  output CF,
  output [15:0] RD2_15_0,
  output [5:0] A_5_0,
  output [5:0] B___Imm__5_0,
  output [1:0] RD1___gt___8_9,
  output [1:0] RD1___gt___10_11,
  output [3:0] JMP_ADDR
);

  wire control_unit_1_p3, control_unit_1_p4, control_unit_1_p5, CPU_CLK, OP;
  wire [3:0] multiplexer_1_out, pc_incrementer_1_p1, PC_out_3_0;
  wire [5:0] _6_bit_alu_1_p5, _6_bit_reg_set_1_b_5_0;
  wire [15:0] _10x16_ram_1_rd1_15_0;

  Multiplexer #(.Bits(4)) multiplexer_1 (
    .sel(control_unit_1_p3), .in_0(pc_incrementer_1_p1), .in_1(JMP_ADDR), .out(multiplexer_1_out));
  and and_1 (CPU_CLK, EN, CLK);
  _4_Bit_Reg PC (.In_3_0(multiplexer_1_out), .CLK(CPU_CLK), .Out_3_0(PC_out_3_0));
  // PC_Incrementer pc_incrementer_1: pin names not known; wires that end beside it: pc_incrementer_1_p1, PC_out_3_0
  _10x16_Ram _10x16_ram_1 (
    .WRD_15_0(WRD_15_0), .WR_3_0(WR_3_0), .WE(WE), .RA1_3_0(PC_out_3_0), .RA2_3_0(RA2_3_0), .CLK(CLK),
    .RD1_15_0({_10x16_ram_1_rd1_15_0[15:12], JMP_ADDR, _10x16_ram_1_rd1_15_0[7:0]}), .RD2_15_0(RD2_15_0));
  _6_Bit_Reg_Set _6_bit_reg_set_1 (
    .WR_1_0(JMP_ADDR[3:2]), .CLK(CPU_CLK), .WRD_5_0(_6_bit_alu_1_p5), .WE(control_unit_1_p4), .A_5_0(A_5_0),
    .B_5_0(_6_bit_reg_set_1_b_5_0), .RA_1_0(JMP_ADDR[3:2]), .RB_1_0(JMP_ADDR[1:0]));
  // _6_Bit_ALU _6_bit_alu_1: pin names not known; wires that end beside it: OP, A_5_0, B___Imm__5_0, CF, _6_bit_alu_1_p5
  // Control_Unit control_unit_1: pin names not known; wires that end beside it: _10x16_ram_1_rd1_15_0[15:12], ZF, control_unit_1_p3, control_unit_1_p4, control_unit_1_p5, OP
  Multiplexer #(.Bits(6)) multiplexer_2 (
    .sel(control_unit_1_p5), .in_0(_6_bit_reg_set_1_b_5_0),
    .in_1({JMP_ADDR[1:0], _10x16_ram_1_rd1_15_0[7:4]}), .out(B___Imm__5_0));

  assign RD1___gt___8_9 = JMP_ADDR[1:0];
  assign RD1___gt___10_11 = JMP_ADDR[3:2];
endmodule
