// Digital circuit Control Unit.dig as structural Verilog
module Control_Unit (
  input  [3:0] Opcode_3_0,
  input  ZF,
  output REG_EN,
  output [1:0] OP_1_0,
  output Im,
  output JMP_EN
);

  wire and_1_out, and_3_out, and_4_out, not_1_out;

  and and_1 (and_1_out, ~Opcode_3_0[3], ~Opcode_3_0[2]);  // And
  and and_2 (Im, ~Opcode_3_0[3], Opcode_3_0[2]);  // And
  not not_1 (not_1_out, REG_EN);
  and and_3 (and_3_out, ~ZF, not_1_out);  // And
  or or_1 (REG_EN, and_1_out, Im);
  and and_4 (and_4_out, REG_EN, ~Opcode_3_0[1], ~Opcode_3_0[0]);  // And
  xor xor_1 (JMP_EN, and_3_out, and_4_out);
  // Pins of 1 and 4 bits meet at Opcode_3_0
  // Pins of 1 and 2 bits meet at Opcode_3_0[1:0]

  assign OP_1_0 = Opcode_3_0[1:0];
endmodule
