// Digital circuit PC Incrementer.dig as structural Verilog
module PC_Incrementer (
  input  [3:0] In_3_0,
  output [3:0] Out_3_0
);

  wire fa_2_cout, fa_3_cout, fa_4_cout;

  FA fa_1 (.Y(1'b0), .X(In_3_0[3]), .S(Out_3_0[3]), .Cin(fa_2_cout));  // open: Cout
  FA fa_2 (.Y(1'b0), .X(In_3_0[2]), .Cout(fa_2_cout), .S(Out_3_0[2]), .Cin(fa_3_cout));
  FA fa_3 (.Y(1'b0), .X(In_3_0[1]), .Cout(fa_3_cout), .S(Out_3_0[1]), .Cin(fa_4_cout));
  FA fa_4 (.Y(1'b1), .X(In_3_0[0]), .Cout(fa_4_cout), .S(Out_3_0[0]), .Cin(1'b0));
  // Pins of 1 and 4 bits meet at Out_3_0
endmodule
